# Fritzing sketch two_wheeler_arduino (saved by Fritzing 0.9.3b)
circuit board: 29.5451cm x 15.4875cm
perfboards: 1

parts:
  Part2 = Arduino Mega 2560 (Rev3)
  Left_A4988 = Pololu A4988 [package=SO16]
  Right_A4988 = Pololu A4988 [package=SO16]
  GY521 = MPU-6050 Board GY-521 [form="♀ (female)" package=THT]
  C1_100uF = Capacitor Polarized [package=panasonic_c]  # not connected
  VCC_7V = Battery
  V_motor_15V = Battery block 9V
  Fuse1_2A = Fuse with Handler [part_number=Htc-15m]
  Fuse2_2A = Fuse with Handler [part_number=Htc-15m]
  R1 = Resistor [tolerance=±5% resistance=1k package="0402 [SMD]"]
  R2 = Resistor [tolerance=±5% resistance=2.2k package="0402 [SMD]"]
  HC_05 = Bluetooth HC-05 Macho

nets:
  N1: Part2.D21/SCL, Part2.SCL, GY521.pin3
  N2: Part2.D20/SDA, Part2.SDA, GY521.pin4
  N3: Part2.D19/RX1, HC_05.TXD
  N4: Part2.D18/TX1, R1.Pin_1
  GND: Part2.GND, Left_A4988.GND#8, Right_A4988.GND#8, GY521.pin2, VCC_7V.-, HC_05.GND
  N5: Part2.D9_PWM, Right_A4988.STEP
  N6: Part2.D8_PWM, Right_A4988.DIR
  5V: Part2.5V, Left_A4988.VDD, GY521.pin1
  N7: Part2.D2_PWM, GY521.pin8
  N8: Part2.D6_PWM, Left_A4988.DIR
  N9: Part2.D7_PWM, Left_A4988.STEP
  N10: Part2.D22, Left_A4988.MS2, Right_A4988.MS2
  N11: Left_A4988.RESET, Left_A4988.SLEEP
  N12: Left_A4988.GND#14, Right_A4988.GND#14, V_motor_15V.-
  N13: Left_A4988.VMOT, Right_A4988.VMOT, Fuse1_2A.Connector1
  N14: Right_A4988.RESET, Right_A4988.SLEEP
  VDD: Right_A4988.VDD, HC_05.VCC
  N15: VCC_7V.+, Fuse2_2A.Connector1
  N16: V_motor_15V.+, Fuse1_2A.Connector2
  N17: R1.Pin_0, R2.Pin_0, HC_05.RXD
  GND_2: R2.Pin_1

notes:
  Bluetooth RX05 (RXD) need 3.3V logic level, hence votage divider
  Voltage on device label (RX_5V) is wrong
  D22 need to break out on stripboard
  15V Power supply breaks out on stripboard
  7V power supply to Arduino (PIN not shown on Arduino)
  Vcc
  Gnd
  SCL
  SDA
  XDA
  XCL
  ADO
  INT
  Wire Color
  Green: A4988 Step and Direction
  Blue: A4988 MS1/2/3
  Orange: MPU6050 SCL/SDA/INT
  Bluetooth Tx/Rx
  White: LED positive (Not shown)

custom parts:
  MPU-6050 Board GY-521: Acelerometro y Giroscopio MPU-6050 Board GY-521
