# Fritzing sketch two_wheeler_rpi_arduino (saved by Fritzing 0.9.3b)
perfboards: 1

parts:
  C1_100uF = Capacitor Polarized [package=panasonic_c]
  V_motor_15V = Battery block 9V
  Fuse1_2A = Fuse with Handler [part_number=Htc-15m]
  rpi4 = Raspberry Pi 4B
  IMU = InvenSense MPU6050
  Left_A4988 = A4988
  Right_A4989 = A4988
  Left_PWM_Gen = AD9833 Module
  Right_PWM_Gen = AD9833 Module

nets:
  N1: C1_100uF.+, Fuse1_2A.Connector1, Left_A4988.VMOT, Right_A4989.VMOT
  N2: C1_100uF.-, V_motor_15V.-, Left_A4988.GND#19, Right_A4989.GND#19
  N3: V_motor_15V.+, Fuse1_2A.Connector2
  VCC: rpi4.3V3, IMU.VCC, Left_PWM_Gen.VCC, Right_PWM_Gen.VCC
  N4: rpi4.GPIO2, IMU.SDA
  VDD: rpi4.5V, Left_A4988.VDD, Right_A4989.VDD
  N5: rpi4.GPIO3, IMU.SCL
  GND: rpi4.GND, IMU.GND, Left_A4988.GND#13, Right_A4989.GND#13, Left_PWM_Gen.DGND, Left_PWM_Gen.AGND, Right_PWM_Gen.DGND, Right_PWM_Gen.AGND
  N6: rpi4.GPIO27, Left_A4988.MS2, Right_A4989.MS2
  N7: rpi4.GPIO24, Left_A4988.DIRECTION
  N8: rpi4.GPIO10, Left_PWM_Gen.SDATA, Right_PWM_Gen.SDATA
  N9: rpi4.GPIO11, Left_PWM_Gen.SCLK, Right_PWM_Gen.SCLK
  N10: rpi4.GPIO8, Left_PWM_Gen.FSYNC
  N11: rpi4.GPIO7, Right_PWM_Gen.FSYNC
  N12: rpi4.GPIO6, Right_A4989.DIRECTION
  N13: Left_A4988.STEP, Left_PWM_Gen.OUT
  N14: Left_A4988.SLEEP, Left_A4988.RESET
  N15: Right_A4989.STEP, Right_PWM_Gen.OUT
  N16: Right_A4989.SLEEP, Right_A4989.RESET

custom parts:
  AD9833 Module: programmable waveform generator
